// Logisim project bramki.circ as structural Verilog: 1 circuit, main circuit main
module main (
  input  CLK,
  input  X,
  output Y1,
  output Y2
);

  wire and_1_out, and_2_out, and_3_out, and_4_out, and_5_out, and_6_out, and_7_out, and_8_out, and_9_out,
       d_ff_1_q, d_ff_1_qn, d_ff_2_q, d_ff_2_qn, d_ff_3_q, d_ff_3_qn, not_1_out, not_2_out, not_3_out,
       not_4_out, not_5_out, not_6_out, or_1_out, or_2_out, or_3_out;

  Shift_Register #(.length(3)) shift_register_1 (
    .in(X), .clk(CLK));  // open: shift, out, load, clr, d0, q0, d1, q1, d2, q2
  not not_1 (not_1_out, d_ff_2_q);
  not not_2 (not_2_out, d_ff_3_q);
  not not_3 (not_3_out, d_ff_1_q);
  not not_4 (not_4_out, X);
  not not_5 (not_5_out, d_ff_1_q);
  not not_6 (not_6_out, d_ff_2_q);
  and and_1 (and_1_out, d_ff_1_q, d_ff_3_q);
  and and_2 (and_2_out, d_ff_1_q, X);
  and and_3 (and_3_out, not_1_out, X, d_ff_3_q);
  and and_4 (and_4_out, d_ff_1_q, not_2_out);
  and and_5 (and_5_out, not_3_out, d_ff_3_q, not_4_out);
  and and_6 (and_6_out, not_5_out, not_6_out, d_ff_3_q);
  or or_1 (or_1_out, and_1_out, and_2_out, and_3_out);
  or or_2 (or_2_out, and_4_out, and_2_out, and_5_out);
  or or_3 (or_3_out, X, and_6_out);
  D_Flip_Flop d_ff_1 (.clk(CLK), .D(or_1_out), .Q(d_ff_1_q), .Qn(d_ff_1_qn));  // open: preset, en, reset
  D_Flip_Flop d_ff_2 (.clk(CLK), .D(or_2_out), .Q(d_ff_2_q), .Qn(d_ff_2_qn));  // open: preset, en, reset
  D_Flip_Flop d_ff_3 (.clk(CLK), .D(or_3_out), .Q(d_ff_3_q), .Qn(d_ff_3_qn));  // open: preset, en, reset
  and and_7 (and_7_out, d_ff_1_q, d_ff_2_qn);
  and and_8 (and_8_out, d_ff_2_qn, d_ff_3_qn);
  and and_9 (and_9_out, d_ff_1_qn, d_ff_2_q);
  or or_4 (Y1, and_7_out, and_8_out);
  or or_5 (Y2, d_ff_3_qn, and_9_out);

  // Notes on the sheet:
  //   przez 3
  //   przez 2
endmodule
