// Logisim project eprom.circ as structural Verilog: 1 circuit, main circuit main
module main (
  input  in_1,
  input  in_2,
  output [2:0] out_3,
  output out_4,
  output out_5,
  output [2:0] out_6,
  output [2:0] out_7,
  output [2:0] out_8
);

  Register #(.width(3)) register_1 (.D(out_8), .Q(out_3), .clk(in_1));  // open: en, clr
  RAM #(.addrWidth(3)) ram_1 (.addr(out_3), .data({out_6, out_7, out_5, out_4}));  // open: sel, clk, ld, clr
  Multiplexer #(.width(3), .disabled(0), .enable("false")) multiplexer_1 (
    .in0(out_6), .in1(out_7), .out(out_8), .sel(in_2));
endmodule
