// Logisim project hazard_dynamiczny.circ as structural Verilog: 1 circuit, main circuit main
module main (
  input  A,
  input  B,
  input  C,
  input  D,
  input  E,
  output Y
);

  wire nand_1_out, nand_2_out, nand_3_out, nand_4_out;

  nand nand_1 (nand_1_out, C, C);
  nand nand_2 (nand_2_out, D, D);
  nand nand_3 (nand_3_out, nand_1_out, nand_2_out, B);
  nand nand_4 (nand_4_out, E, nand_3_out);
  nand nand_5 (Y, nand_4_out, A);
endmodule
